# Fritzing sketch schematique portail (saved by Fritzing 0.9.3b)
circuit board: 8.46667cm x 5.64444cm
breadboards: 1

parts:
  Composant1 = Arduino Nano (Rev3.0)
  Composant2 = Bluetooth HC-05 Macho
  Q1 = Basic FET N-Channel [package="TO220 [THT]"]
  U1 = SIP - 2 pins [chip_label=IC package="SIP (Single Inline) [THT]"]

nets:
  GND: Composant1.GND, Composant2.GND
  N1: Composant1.D9, Q1.gate
  N2: Composant1.D10, Composant2.TXD
  N3: Composant1.D11/MOSI, Composant2.RXD
  5V: Composant1.5V, Composant2.VCC
  GND_2: Q1.drain, U1.pin1
  N4: Q1.source, U1.pin2
